// Logisim project dl.11 multi.circ as structural Verilog: 1 circuit, main circuit main
module main (
  input  s1,
  input  s2,
  input  _10,
  input  c,
  input  c_prime,
  input  _11,
  input  _0_Logic_low,
  input  _12,
  input  _1_Logic_hight,
  input  AB,
  input  _13,
  output out_12,
  output \F_A_B_C__Σ_1_2_6_7 
);

  wire and_1_out, and_2_out, and_3_out, and_4_out, not_1_out, not_2_out, not_3_out;

  not not_1 (not_1_out, s2);
  not not_2 (not_2_out, s1);
  and and_1 (and_1_out, not_2_out, not_1_out, _10);
  and and_2 (and_2_out, not_2_out, not_1_out, _11);
  and and_3 (and_3_out, s1, not_1_out, _12);
  and and_4 (and_4_out, s1, s2, _13);
  or or_1 (out_12, and_1_out, and_2_out, and_3_out, and_4_out);
  not not_3 (not_3_out, c_prime);
  Multiplexer multiplexer_1 (.in0(not_3_out), .in1(_1_Logic_hight), .out(\F_A_B_C__Σ_1_2_6_7 ), .sel(AB));  // open: en
endmodule
